# Fritzing sketch Door_status (saved by Fritzing 0.9.3b)
breadboards: 1

parts:
  元件1 = Arduino Mega 2560 (Rev3)
  R1 = Rotary Potentiometer (Small) [maximum_resistance=100kΩ package=THT]
  LCD1 = LCD screen
  R2 = Resistor [tolerance=±5% resistance=330 package=THT]
  元件2 = HC-SR501 Body Sensor Module
  R3 = Resistor [tolerance=±5% resistance=10k package=THT]
  R4 = Photocell (LDR) [package=THT]

nets:
  N1: 元件1.A0, R3.Pin_1, R4.pin_0
  N2: 元件1.D12_PWM, LCD1.E
  N3: 元件1.D11_PWM, LCD1.RS
  5V: 元件1.5V, R1.leg2, LCD1.VDD, R2.Pin_1, 元件2.VCC, R3.Pin_0
  GND: 元件1.GND, R1.leg1, LCD1.VSS, LCD1.R/W, LCD1.LED-, 元件2.GND, R4.pin_1
  N4: 元件1.D3_PWM, LCD1.DB7
  N5: 元件1.D4_PWM, LCD1.DB6
  N6: 元件1.D5_PWM, LCD1.DB5
  N7: 元件1.D6_PWM, LCD1.DB4
  N8: 元件1.D7_PWM, 元件2.OUT
  N9: R1.wiper, LCD1.V0
  N10: LCD1.LED+, R2.Pin_0

custom parts:
  HC-SR501 Body Sensor Module: Pyroelectric Infrared PIR Motion Sensor Detector Module
