# Fritzing sketch schaltung (saved by Fritzing 0.9.3b)
circuit board: 8.46667cm x 5.64444cm
breadboards: 1

parts:
  元件1 = Arduino Mega 2560 (Rev3)
  S1 = Pushbutton [package="[THT]"]
  R1 = Resistor [tolerance=±5% resistance=10k package=THT]
  LED1 = LED - 5mm [color="Red (633nm)" package="5 mm [THT]"]

nets (from the breadboard view):
  N1: 元件1.GND, R1.Pin_1, LED1.cathode
  N2: 元件1.D13_PWM, LED1.anode
  N3: 元件1.5V, S1.Pin_3, S1.Pin_4
  N4: 元件1.D2_PWM, S1.Pin_1, S1.Pin_2, R1.Pin_0

// code stored in the sketch: LED_Schalter.ino
const byte led = 13;
const byte sw = 2;
byte click = 0;
boolean lastState = 0;
boolean toggle = 0;
void setup() {
  pinMode(led,OUTPUT);
  pinMode(sw,INPUT);
  lastState = digitalRead(sw);
}

void loop() {
  boolean b1 = digitalRead(sw);
  if (b1 != lastState)
    {
      delay (20);
      boolean b2 = digitalRead (sw);
      if (b1 == b2)
        {
          lastState = b1;
          click++;
        }
    }
   if (click == 2)
    {
      click = 0;
      toggle = !toggle;
      digitalWrite (led,toggle);
    }
}
