# Fritzing sketch Nachtlicht (saved by Fritzing 0.9.3b)
breadboards: 1

parts:
  元件1 = Arduino Mega 2560 (Rev3)
  R1 = Photocell (LDR) [package=THT]
  R2 = Resistor [tolerance=±5% resistance=10k package=THT]

nets:
  N1: 元件1.A0, R1.pin_0, R2.Pin_1
  N2: 元件1.5V, R2.Pin_0
  N3: 元件1.GND, R1.pin_1
