# Fritzing sketch Projekt-Code (saved by Fritzing 0.9.3b)
breadboards: 1

parts:
  元件1 = Arduino Mega 2560 (Rev3)
  R1 = Rotary Potentiometer (Small) [maximum_resistance=100kΩ package=THT]
  LCD1 = LCD screen
  R2 = Resistor [tolerance=±5% resistance=330 package=THT]
  LED1 = LED - 5mm [color="Yellow (585nm)" package="5 mm [THT]"]
  R3 = Resistor [tolerance=±5% resistance=220 package=THT]
  hc-sr1 = hc-sr04
  元件2 = HC-SR501 Body Sensor Module
  R4 = Resistor [tolerance=±5% resistance=220 package=THT]
  LED2 = LED - 5mm [color="Red (633nm)" package="5 mm [THT]"]

nets:
  N1: 元件1.D13_PWM, LED1.anode
  N2: 元件1.D12_PWM, LCD1.E
  N3: 元件1.D11_PWM, LCD1.RS
  N4: 元件1.D10_PWM, hc-sr1.Trig
  N5: 元件1.D9_PWM, hc-sr1.Echo
  N6: 元件1.D8_PWM, LED2.anode
  VCC: 元件1.5V, R1.leg2, LCD1.VDD, R2.Pin_1, hc-sr1.VCC, 元件2.VCC
  GND: 元件1.GND, R1.leg1, LCD1.VSS, LCD1.R/W, LCD1.LED-, R3.Pin_0, hc-sr1.GND, 元件2.GND, R4.Pin_0
  N7: 元件1.D3_PWM, LCD1.DB7
  N8: 元件1.D4_PWM, LCD1.DB6
  N9: 元件1.D5_PWM, LCD1.DB5
  N10: 元件1.D6_PWM, LCD1.DB4
  N11: 元件1.D7_PWM, 元件2.OUT
  N12: R1.wiper, LCD1.V0
  N13: LCD1.LED+, R2.Pin_0
  N14: LED1.cathode, R3.Pin_1
  N15: R4.Pin_1, LED2.cathode

custom parts:
  HC-SR501 Body Sensor Module: Pyroelectric Infrared PIR Motion Sensor Detector Module
